// Digital circuit simulation.dig as structural Verilog
module simulation (
  input  NE555___CLK,
  input  Int_NE555,
  output CLR__not_used,
  output not_CLR,
  output CLK,
  output not_CLK,
  output CPC,
  output LIR,
  output not_ERAM,
  output not_EPC_RAM,
  output not_NOP,
  output LACC,
  output not_EACC,
  output HLT,
  output LMAR_L,
  output LMAR_H,
  output not_EMAR,
  output not_WRAM,
  output not_LPC_H,
  output not_LPC_L,
  output LRALU_IN,
  output LRALU_OUT,
  output ALUS0,
  output ALUS1,
  output ALUS2,
  output ALUS3,
  output ALUCN,
  output ALUM,
  output not_ERALU_OUT,
  output LOUT,
  output not_EX,
  output LX,
  output not_EY,
  output LY,
  output LC,
  output CHKZ,
  output CHKC,
  output not_CLC,
  output not_SEC,
  output LZ,
  output not_CSP,
  output SPD,
  output not_ESP,
  output not_EPC_L,
  output not_EPC_H,
  output CHKI,
  output not_DIS_I,
  output not_ENA_I,
  output not_ETMP,
  output LTMP,
  output LO,
  output CHKO,
  output not_EFR_out,
  output EFR_in,
  output Enable_Int,
  output A1,
  output A2,
  output A3,
  output A4,
  output A5,
  output A6,
  output A7,
  output A8
);

  wire _7400_1_pin3, _7400_1_pin5, _7400_1_pin8, _7400_1_pin10, _7400_1_pin11, _7400_1_pin12, _7404_1_pin9,
       _7408_1_pin1, _7408_1_pin2, _7408_1_pin3, _7408_1_pin6, _7408_1_pin8, _7408_1_pin10, _7408_2_pin6,
       _7408_2_pin9, _7408_2_pin10, _7408_2_pin11, _7408_3_pin6, _7408_3_pin8, _7432_1_pin9, _7432_1_pin10,
       _74161_1_pin15, _74161_2_pin15, _74161_3_pin15, _74191_1_pin13, ALU_H_pin2, ALU_H_pin7, ALU_H_pin9,
       ALU_H_pin10, ALU_H_pin11, ALU_L_pin2, ALU_L_pin9, ALU_L_pin10, ALU_L_pin11, CLOCK_BUF_C27_pin2,
       CLOCK_BUF_C27_pin12, CLOCK_BUF_C27_pin13, Control_Word__7_p5, Control_Word__7_p7, Control_Word__7_p9,
       Control_Word__7_p10, Control_Word__7_p11, Control_Word__7_p13, Control_Word__7_p14,
       Control_Word__7_p15, Control_Word__7_p16, Control_Word__7_p17, Control_Word__7_p18,
       Control_Word__7_p19, Control_Word__7_p20, Debouncer_C24_pin8, Debouncer_C24_pin10, Debouncer_C26_pin2,
       Debouncer_C26_pin3, Debouncer_C26_pin8, Debouncer_C26_pin10, Debouncer_C26_pin11, Debouncer_C26_pin12,
       FR_in_pin9, FR_in_pin11, FR_in_pin12, FR_in_pin14, I_pin9, IC_H_pin1, IC_H_pin10, MAR_H_pin2,
       MAR_H_pin5, MAR_H_pin6, MAR_H_pin9, MAR_H_pin12, MAR_H_pin15, MAR_H_pin16, MAR_L_pin2, MAR_L_pin5,
       MAR_L_pin6, MAR_L_pin9, MAR_L_pin12, MAR_L_pin15, MAR_L_pin16, MAR_L_pin19, PUSH_CLEAR_p2,
       PUSH_CLEAR_p3, PUSH_CLEAR_p4, PUSH_SINGLE_STEP_p2, PUSH_SINGLE_STEP_p3, RALU_IN_pin5, RALU_IN_pin6,
       RALU_IN_pin9, RALU_IN_pin15, RALU_IN_pin16, RALU_IN_pin19, RALU_OUT_pin8, RALU_OUT_pin18,
       SW_MANUAL_AUTO_p2;
  wire [3:0] _74161_1_pin14, _74161_2_pin14, _74161_3_pin14, _74161_4_pin14, _74245_6_pin5, _74245_6_pin9,
       FR_OUT_pin14, FR_OUT_pin18, OUT_pin2, OUT_pin19;

  // _28c64 Control_Word__7: pin names not known; wires that end beside it: 1'b0, A3, A2, A1, Control_Word__7_p5, A8, Control_Word__7_p7, 1'b0, Control_Word__7_p9, Control_Word__7_p10, Control_Word__7_p11, 1'b0, Control_Word__7_p13, Control_Word__7_p14, Control_Word__7_p15, Control_Word__7_p16, Control_Word__7_p17, Control_Word__7_p18, Control_Word__7_p19, Control_Word__7_p20, 1'b1, 1'b1
  // _28c64 Control_Word__6: pin names not known; wires that end beside it: 1'b0, not_ETMP, not_ENA_I, not_DIS_I, Control_Word__7_p5, EFR_in, Control_Word__7_p7, 1'b0, Control_Word__7_p9, Control_Word__7_p10, Control_Word__7_p11, 1'b0, Control_Word__7_p13, Control_Word__7_p14, Control_Word__7_p15, Control_Word__7_p16, Control_Word__7_p17, Control_Word__7_p18, Control_Word__7_p19, Control_Word__7_p20, 1'b1, 1'b1
  // _28c64 Control_Word__5: pin names not known; wires that end beside it: 1'b0, not_CSP, LZ, not_SEC, Control_Word__7_p5, CHKI, Control_Word__7_p7, 1'b0, Control_Word__7_p9, Control_Word__7_p10, Control_Word__7_p11, 1'b0, Control_Word__7_p13, Control_Word__7_p14, Control_Word__7_p15, Control_Word__7_p16, Control_Word__7_p17, Control_Word__7_p18, Control_Word__7_p19, Control_Word__7_p20, 1'b1, 1'b1
  _7408 _7408_1 (
    .pin1(_7408_1_pin1), .pin2(_7408_1_pin2), .pin3(_7408_1_pin3), .pin4(CLK), .pin5(LO),
    .pin6(_7408_1_pin6), .pin7(1'b0), .pin8(_7408_1_pin8), .pin9(Enable_Int), .pin10(_7408_1_pin10),
    .pin11(_7408_1_pin10), .pin12(CLK), .pin13(CHKI), .pin14(1'b1));
  _7474 I (
    .pin1(not_DIS_I), .pin2(1'b1), .pin3(1'b0), .pin4(not_ENA_I), .pin5(Enable_Int), .pin7(1'b0),
    .pin9(I_pin9), .pin10(1'b1), .pin11(Int_NE555), .pin12(1'b1), .pin13(not_ENA_I), .pin14(1'b1));  // open: pin6, pin8
  // _28c64 Control_Word__4: pin names not known; wires that end beside it: 1'b0, not_EY, LX, not_EX, Control_Word__7_p5, not_CLC, Control_Word__7_p7, 1'b0, Control_Word__7_p9, Control_Word__7_p10, Control_Word__7_p11, 1'b0, Control_Word__7_p13, Control_Word__7_p14, Control_Word__7_p15, Control_Word__7_p16, Control_Word__7_p17, Control_Word__7_p18, Control_Word__7_p19, Control_Word__7_p20, 1'b1, 1'b1
  _74157 FR_in (
    .pin1(EFR_in), .pin2(1'b1), .pin3(1'b1), .pin5(1'b1), .pin6(1'b1), .pin8(1'b0), .pin9(FR_in_pin9),
    .pin10(FR_OUT_pin18[2]), .pin11(FR_in_pin11), .pin12(FR_in_pin12), .pin13(FR_OUT_pin18[3]),
    .pin14(FR_in_pin14), .pin15(1'b0), .pin16(1'b1));  // open: pin4, pin7
  _7400 _7400_1 (
    .pin1(I_pin9), .pin2(_7408_1_pin8), .pin3(_7400_1_pin3), .pin4(CHKO), .pin5(_7400_1_pin5),
    .pin6(_7408_1_pin2), .pin7(1'b0), .pin8(_7400_1_pin8), .pin9(CHKC), .pin10(_7400_1_pin10),
    .pin11(_7400_1_pin11), .pin12(_7400_1_pin12), .pin13(CHKZ), .pin14(1'b1));
  _7432 _7432_1 (
    .pin1(1'b0), .pin2(1'b0), .pin4(1'b0), .pin5(1'b0), .pin7(1'b0), .pin8(FR_in_pin14), .pin9(_7432_1_pin9),
    .pin10(_7432_1_pin10), .pin12(1'b1), .pin13(1'b1), .pin14(1'b1));  // open: pin3, pin6, pin11
  _7474 O (
    .pin1(1'b1), .pin2(1'b1), .pin3(1'b0), .pin4(1'b1), .pin7(1'b0), .pin8(_7400_1_pin5), .pin10(1'b1),
    .pin11(_7408_1_pin6), .pin12(FR_in_pin11), .pin13(1'b1), .pin14(1'b1));  // open: pin5, pin6, pin9
  _74245 FR_OUT (
    .pin1(1'b1), .pin2(1'b1), .pin3(1'b1), .pin4(_7400_1_pin10), .pin5(_7400_1_pin12), .pin6(1'b1),
    .pin7(1'b1), .pin8(1'b1), .pin9(1'b1), .pin10(1'b0), .pin11(FR_OUT_pin14[3]), .pin12(FR_OUT_pin14[2]),
    .pin13(FR_OUT_pin14[1]), .pin14(FR_OUT_pin14[0]), .pin15(FR_OUT_pin18[3]), .pin16(FR_OUT_pin18[2]),
    .pin17(FR_OUT_pin18[1]), .pin18(FR_OUT_pin18[0]), .pin19(not_EFR_out), .pin20(1'b1));
  Seven_Seg_Hex seven_seg_hex_1 (.d(FR_OUT_pin14), .dp(1'b0));
  _74163 IC_H (
    .pin1(IC_H_pin1), .pin2(not_CLK), .pin3(1'b1), .pin4(1'b0), .pin5(1'b0), .pin6(1'b0), .pin7(1'b1),
    .pin8(1'b0), .pin9(_7408_1_pin3), .pin10(IC_H_pin10), .pin14(Control_Word__7_p13), .pin16(1'b1));  // open: pin11, pin12, pin13, pin15
  Seven_Seg_Hex seven_seg_hex_2 (.d(FR_OUT_pin18), .dp(1'b0));
  _7408 _7408_2 (
    .pin1(_7400_1_pin11), .pin2(_7400_1_pin8), .pin3(_7408_1_pin1), .pin4(CLK), .pin5(LZ),
    .pin6(_7408_2_pin6), .pin7(1'b0), .pin8(_7432_1_pin9), .pin9(_7408_2_pin9), .pin10(_7408_2_pin10),
    .pin11(_7408_2_pin11), .pin12(CLK), .pin13(LC), .pin14(1'b1));
  _7474 Z___C (
    .pin1(1'b1), .pin2(FR_in_pin12), .pin3(_7408_2_pin6), .pin4(1'b1), .pin5(_7400_1_pin12), .pin7(1'b0),
    .pin9(_7400_1_pin10), .pin10(not_SEC), .pin11(_7408_2_pin11), .pin12(FR_in_pin9), .pin13(not_CLC),
    .pin14(1'b1));  // open: pin6, pin8
  _74163 IC_L (
    .pin1(IC_H_pin1), .pin2(not_CLK), .pin3(1'b0), .pin4(1'b0), .pin5(1'b0), .pin6(1'b0), .pin7(1'b1),
    .pin8(1'b0), .pin9(_7408_1_pin3), .pin10(1'b1), .pin11(Control_Word__7_p11), .pin12(Control_Word__7_p9),
    .pin13(Control_Word__7_p7), .pin14(Control_Word__7_p5), .pin15(IC_H_pin10), .pin16(1'b1));
  // _28c64 Control_Word__3: pin names not known; wires that end beside it: 1'b0, ALUS2, ALUS1, ALUS0, Control_Word__7_p5, LOUT, Control_Word__7_p7, 1'b0, Control_Word__7_p9, Control_Word__7_p10, Control_Word__7_p11, 1'b0, Control_Word__7_p13, Control_Word__7_p14, Control_Word__7_p15, Control_Word__7_p16, Control_Word__7_p17, Control_Word__7_p18, Control_Word__7_p19, Control_Word__7_p20, 1'b1, 1'b1, 1'b0
  Seven_Seg_Hex seven_seg_hex_3 (.d(_74161_4_pin14), .dp(1'b0));
  Seven_Seg_Hex seven_seg_hex_4 (.d(_74161_3_pin14), .dp(1'b0));
  Seven_Seg_Hex seven_seg_hex_5 (.d(_74161_2_pin14), .dp(1'b0));
  Seven_Seg_Hex seven_seg_hex_6 (.d(_74161_1_pin14), .dp(1'b0));
  _7408 _7408_3 (
    .pin1(not_CLR), .pin2(not_NOP), .pin3(IC_H_pin1), .pin4(not_CLR), .pin5(_7400_1_pin3),
    .pin6(_7408_3_pin6), .pin7(1'b0), .pin8(_7408_3_pin8), .pin9(LIR), .pin10(not_CLK), .pin12(1'b1),
    .pin13(1'b1), .pin14(1'b1));  // open: pin11
  // SwitchDT PUSH_CLEAR: pin names not known; wires that end beside it: 1'b0, PUSH_CLEAR_p2, PUSH_CLEAR_p3, PUSH_CLEAR_p4
  // SwitchDT PUSH_SINGLE_STEP: pin names not known; wires that end beside it: 1'b0, PUSH_SINGLE_STEP_p2, PUSH_SINGLE_STEP_p3
  // SwitchDT SW_MANUAL_AUTO: pin names not known; wires that end beside it: 1'b0, SW_MANUAL_AUTO_p2
  // _28c64 Control_Word__2: pin names not known; wires that end beside it: not_EMAR, LMAR_H, LMAR_L, Control_Word__7_p5, LRALU_OUT, Control_Word__7_p7, 1'b0, Control_Word__7_p9, Control_Word__7_p10, Control_Word__7_p11, 1'b0, Control_Word__7_p13, Control_Word__7_p14, Control_Word__7_p15, Control_Word__7_p16, Control_Word__7_p17, Control_Word__7_p18, Control_Word__7_p19, Control_Word__7_p20, 1'b1, 1'b1, 1'b0, not_EPC_RAM
  _74181 ALU_L (
    .pin1(FR_OUT_pin18[0]), .pin2(ALU_L_pin2), .pin3(ALUS3), .pin4(ALUS2), .pin5(ALUS1), .pin6(ALUS0),
    .pin7(ALUCN), .pin8(ALUM), .pin9(ALU_L_pin9), .pin10(ALU_L_pin10), .pin11(ALU_L_pin11), .pin12(1'b0));  // open: pin13, pin14, pin15, pin16, pin17, pin18, pin19, pin20, pin21, pin22, pin23, pin24
  _74181 ALU_H (
    .pin1(FR_OUT_pin14[0]), .pin2(ALU_H_pin2), .pin3(ALUS3), .pin4(ALUS2), .pin5(ALUS1), .pin6(ALUS0),
    .pin7(ALU_H_pin7), .pin8(ALUM), .pin9(ALU_H_pin9), .pin10(ALU_H_pin10), .pin11(ALU_H_pin11), .pin12(1'b0));  // open: pin13, pin14, pin15, pin16, pin17, pin18, pin19, pin20, pin21, pin22, pin23, pin24
  _7404 _7404_1 (
    .pin1(1'b0), .pin3(1'b0), .pin5(1'b0), .pin7(1'b0), .pin8(_7432_1_pin10), .pin9(_7404_1_pin9),
    .pin11(1'b1), .pin13(1'b1), .pin14(1'b1));  // open: pin2, pin4, pin6, pin10, pin12
  PullUp pullup_1 (.out(PUSH_CLEAR_p2));
  PullUp pullup_2 (.out(PUSH_CLEAR_p3));
  PullUp pullup_3 (.out(PUSH_SINGLE_STEP_p2));
  PullUp pullup_4 (.out(PUSH_CLEAR_p4));
  PullUp pullup_5 (.out(SW_MANUAL_AUTO_p2));
  PullUp pullup_6 (.out(PUSH_SINGLE_STEP_p3));
  _7400 Debouncer_C24 (
    .pin1(PUSH_CLEAR_p2), .pin2(CLR__not_used), .pin3(not_CLR), .pin4(not_CLR), .pin5(PUSH_CLEAR_p3),
    .pin6(CLR__not_used), .pin7(1'b0), .pin8(Debouncer_C24_pin8), .pin9(PUSH_SINGLE_STEP_p2),
    .pin10(Debouncer_C24_pin10), .pin11(Debouncer_C24_pin10), .pin12(Debouncer_C24_pin8),
    .pin13(PUSH_CLEAR_p4), .pin14(1'b1));
  _7400 Debouncer_C26 (
    .pin1(PUSH_SINGLE_STEP_p3), .pin2(Debouncer_C26_pin2), .pin3(Debouncer_C26_pin3),
    .pin4(Debouncer_C26_pin3), .pin5(SW_MANUAL_AUTO_p2), .pin6(Debouncer_C26_pin2), .pin7(1'b0),
    .pin8(Debouncer_C26_pin8), .pin9(Debouncer_C26_pin2), .pin10(Debouncer_C26_pin10),
    .pin11(Debouncer_C26_pin11), .pin12(Debouncer_C26_pin12), .pin13(Debouncer_C26_pin8), .pin14(1'b1));
  _74688 Z_BUS (
    .pin1(1'b0), .pin2(1'b0), .pin3(FR_OUT_pin18[0]), .pin4(1'b0), .pin5(FR_OUT_pin18[1]), .pin6(1'b0),
    .pin7(FR_OUT_pin18[2]), .pin8(1'b0), .pin9(FR_OUT_pin18[3]), .pin10(1'b0), .pin11(1'b0),
    .pin12(FR_OUT_pin14[0]), .pin13(1'b0), .pin14(FR_OUT_pin14[1]), .pin15(1'b0), .pin16(FR_OUT_pin14[2]),
    .pin17(1'b0), .pin18(FR_OUT_pin14[3]), .pin19(_7404_1_pin9), .pin20(1'b1));
  // _28c64 Control_Word__1: pin names not known; wires that end beside it: not_ERAM, LIR, Control_Word__7_p5, not_NOP, Control_Word__7_p7, 1'b0, Control_Word__7_p9, Control_Word__7_p10, Control_Word__7_p11, 1'b0, Control_Word__7_p13, Control_Word__7_p14, Control_Word__7_p15, Control_Word__7_p16, Control_Word__7_p17, Control_Word__7_p18, Control_Word__7_p19, Control_Word__7_p20, 1'b1, 1'b1
  _7410 C25 (
    .pin1(HLT), .pin2(Debouncer_C24_pin10), .pin3(1'b1), .pin4(1'b1), .pin5(1'b1), .pin7(1'b0), .pin9(1'b1),
    .pin10(1'b1), .pin11(1'b1), .pin12(Debouncer_C26_pin12), .pin13(Debouncer_C26_pin3), .pin14(1'b1));  // open: pin6, pin8
  _74107 C29 (
    .pin1(HLT), .pin3(Debouncer_C26_pin10), .pin4(HLT), .pin7(1'b0), .pin8(1'b0), .pin9(1'b0), .pin10(1'b0),
    .pin11(1'b0), .pin12(NE555___CLK), .pin13(not_CLR), .pin14(1'b1));  // open: pin2, pin5, pin6
  _7404 CLOCK_BUF_C27 (
    .pin1(Debouncer_C26_pin11), .pin2(CLOCK_BUF_C27_pin2), .pin3(CLOCK_BUF_C27_pin2), .pin4(CLK),
    .pin5(Debouncer_C26_pin11), .pin6(not_CLK), .pin7(1'b0), .pin9(1'b1), .pin11(1'b1),
    .pin12(CLOCK_BUF_C27_pin12), .pin13(CLOCK_BUF_C27_pin13), .pin14(1'b1));  // open: pin8, pin10
  _74273 IR (
    .pin1(_7408_3_pin6), .pin2(Control_Word__7_p15), .pin3(FR_OUT_pin18[0]), .pin4(FR_OUT_pin18[1]),
    .pin5(Control_Word__7_p17), .pin6(Control_Word__7_p19), .pin7(FR_OUT_pin18[2]), .pin8(FR_OUT_pin18[3]),
    .pin9(Control_Word__7_p18), .pin10(1'b0), .pin11(_7408_3_pin8), .pin12(Control_Word__7_p16),
    .pin13(FR_OUT_pin14[0]), .pin14(FR_OUT_pin14[1]), .pin15(Control_Word__7_p10),
    .pin16(Control_Word__7_p14), .pin17(FR_OUT_pin14[2]), .pin18(FR_OUT_pin14[3]),
    .pin19(Control_Word__7_p20), .pin20(1'b1));
  _74373 ACC (
    .pin1(not_EACC), .pin2(FR_OUT_pin18[0]), .pin3(FR_OUT_pin18[0]), .pin4(FR_OUT_pin18[1]),
    .pin5(FR_OUT_pin18[1]), .pin6(FR_OUT_pin18[2]), .pin7(FR_OUT_pin18[2]), .pin8(FR_OUT_pin18[3]),
    .pin9(FR_OUT_pin18[3]), .pin10(1'b0), .pin11(LACC), .pin12(FR_OUT_pin14[0]), .pin13(FR_OUT_pin14[0]),
    .pin14(FR_OUT_pin14[1]), .pin15(FR_OUT_pin14[1]), .pin16(FR_OUT_pin14[2]), .pin17(FR_OUT_pin14[2]),
    .pin18(FR_OUT_pin14[3]), .pin19(FR_OUT_pin14[3]), .pin20(1'b1));
  _74373 RALU_IN (
    .pin1(1'b0), .pin2(ALU_L_pin2), .pin3(FR_OUT_pin18[0]), .pin4(FR_OUT_pin18[1]), .pin5(RALU_IN_pin5),
    .pin6(RALU_IN_pin6), .pin7(FR_OUT_pin18[2]), .pin8(FR_OUT_pin18[3]), .pin9(RALU_IN_pin9), .pin10(1'b0),
    .pin11(LRALU_IN), .pin12(ALU_H_pin2), .pin13(FR_OUT_pin14[0]), .pin14(FR_OUT_pin14[1]),
    .pin15(RALU_IN_pin15), .pin16(RALU_IN_pin16), .pin17(FR_OUT_pin14[2]), .pin18(FR_OUT_pin14[3]),
    .pin19(RALU_IN_pin19), .pin20(1'b1));
  _74373 RALU_OUT (
    .pin1(not_ERALU_OUT), .pin2(FR_OUT_pin18[0]), .pin3(ALU_L_pin9), .pin4(ALU_L_pin10),
    .pin5(FR_OUT_pin18[1]), .pin6(FR_OUT_pin18[2]), .pin7(ALU_L_pin11), .pin8(RALU_OUT_pin8),
    .pin9(FR_OUT_pin18[3]), .pin10(1'b0), .pin11(LRALU_OUT), .pin12(FR_OUT_pin14[0]), .pin13(ALU_H_pin9),
    .pin14(ALU_H_pin10), .pin15(FR_OUT_pin14[1]), .pin16(FR_OUT_pin14[2]), .pin17(ALU_H_pin11),
    .pin18(RALU_OUT_pin18), .pin19(FR_OUT_pin14[3]), .pin20(1'b1));
  _74161 _74161_1 (
    .pin1(not_CLR), .pin2(not_CLK), .pin3(FR_OUT_pin18[0]), .pin4(FR_OUT_pin18[1]), .pin5(FR_OUT_pin18[2]),
    .pin6(FR_OUT_pin18[3]), .pin7(CPC), .pin8(1'b0), .pin9(not_LPC_L), .pin10(1'b1),
    .pin11(_74161_1_pin14[3]), .pin12(_74161_1_pin14[2]), .pin13(_74161_1_pin14[1]),
    .pin14(_74161_1_pin14[0]), .pin15(_74161_1_pin15), .pin16(1'b1));
  _74161 _74161_2 (
    .pin1(not_CLR), .pin2(not_CLK), .pin3(FR_OUT_pin14[0]), .pin4(FR_OUT_pin14[1]), .pin5(FR_OUT_pin14[2]),
    .pin6(FR_OUT_pin14[3]), .pin7(CPC), .pin8(1'b0), .pin9(not_LPC_L), .pin10(_74161_1_pin15),
    .pin11(_74161_2_pin14[3]), .pin12(_74161_2_pin14[2]), .pin13(_74161_2_pin14[1]),
    .pin14(_74161_2_pin14[0]), .pin15(_74161_2_pin15), .pin16(1'b1));
  _74161 _74161_3 (
    .pin1(not_CLR), .pin2(not_CLK), .pin3(FR_OUT_pin18[0]), .pin4(FR_OUT_pin18[1]), .pin5(FR_OUT_pin18[2]),
    .pin6(FR_OUT_pin18[3]), .pin7(CPC), .pin8(1'b0), .pin9(not_LPC_H), .pin10(_74161_2_pin15),
    .pin11(_74161_3_pin14[3]), .pin12(_74161_3_pin14[2]), .pin13(_74161_3_pin14[1]),
    .pin14(_74161_3_pin14[0]), .pin15(_74161_3_pin15), .pin16(1'b1));
  _74161 _74161_4 (
    .pin1(not_CLR), .pin2(not_CLK), .pin3(FR_OUT_pin14[0]), .pin4(FR_OUT_pin14[1]), .pin5(FR_OUT_pin14[2]),
    .pin6(FR_OUT_pin14[3]), .pin7(CPC), .pin8(1'b0), .pin9(not_LPC_H), .pin10(_74161_3_pin15),
    .pin11(_74161_4_pin14[3]), .pin12(_74161_4_pin14[2]), .pin13(_74161_4_pin14[1]),
    .pin14(_74161_4_pin14[0]), .pin16(1'b1));  // open: pin15
  _74373 MAR_L (
    .pin1(not_EMAR), .pin2(MAR_L_pin2), .pin3(FR_OUT_pin18[0]), .pin4(FR_OUT_pin18[1]), .pin5(MAR_L_pin5),
    .pin6(MAR_L_pin6), .pin7(FR_OUT_pin18[2]), .pin8(FR_OUT_pin18[3]), .pin9(MAR_L_pin9), .pin10(1'b0),
    .pin11(LMAR_L), .pin12(MAR_L_pin12), .pin13(FR_OUT_pin14[0]), .pin14(FR_OUT_pin14[1]),
    .pin15(MAR_L_pin15), .pin16(MAR_L_pin16), .pin17(FR_OUT_pin14[2]), .pin18(FR_OUT_pin14[3]),
    .pin19(MAR_L_pin19), .pin20(1'b1));
  _74373 MAR_H (
    .pin1(not_EMAR), .pin2(MAR_H_pin2), .pin3(FR_OUT_pin18[0]), .pin4(FR_OUT_pin18[1]), .pin5(MAR_H_pin5),
    .pin6(MAR_H_pin6), .pin7(FR_OUT_pin18[2]), .pin8(FR_OUT_pin18[3]), .pin9(MAR_H_pin9), .pin10(1'b0),
    .pin11(LMAR_H), .pin12(MAR_H_pin12), .pin13(FR_OUT_pin14[0]), .pin14(FR_OUT_pin14[1]),
    .pin15(MAR_H_pin15), .pin16(MAR_H_pin16), .pin17(FR_OUT_pin14[2]), .pin18(FR_OUT_pin14[3]),
    .pin19(CLOCK_BUF_C27_pin13), .pin20(1'b1));
  _74373 OUT (
    .pin1(1'b0), .pin2(OUT_pin2[0]), .pin3(FR_OUT_pin18[0]), .pin4(FR_OUT_pin18[1]), .pin5(OUT_pin2[1]),
    .pin6(OUT_pin2[2]), .pin7(FR_OUT_pin18[2]), .pin8(FR_OUT_pin18[3]), .pin9(OUT_pin2[3]), .pin10(1'b0),
    .pin11(LOUT), .pin12(OUT_pin19[0]), .pin13(FR_OUT_pin14[0]), .pin14(FR_OUT_pin14[1]),
    .pin15(OUT_pin19[1]), .pin16(OUT_pin19[2]), .pin17(FR_OUT_pin14[2]), .pin18(FR_OUT_pin14[3]),
    .pin19(OUT_pin19[3]), .pin20(1'b1));
  _74373 X (
    .pin1(not_EX), .pin2(FR_OUT_pin18[0]), .pin3(FR_OUT_pin18[0]), .pin4(FR_OUT_pin18[1]),
    .pin5(FR_OUT_pin18[1]), .pin6(FR_OUT_pin18[2]), .pin7(FR_OUT_pin18[2]), .pin8(FR_OUT_pin18[3]),
    .pin9(FR_OUT_pin18[3]), .pin10(1'b0), .pin11(LX), .pin12(FR_OUT_pin14[0]), .pin13(FR_OUT_pin14[0]),
    .pin14(FR_OUT_pin14[1]), .pin15(FR_OUT_pin14[1]), .pin16(FR_OUT_pin14[2]), .pin17(FR_OUT_pin14[2]),
    .pin18(FR_OUT_pin14[3]), .pin19(FR_OUT_pin14[3]), .pin20(1'b1));
  Seven_Seg_Hex seven_seg_hex_7 (.d(OUT_pin19), .dp(1'b0));
  Seven_Seg_Hex seven_seg_hex_8 (.d(OUT_pin2), .dp(1'b0));
  _74373 Y (
    .pin1(not_EY), .pin2(FR_OUT_pin18[0]), .pin3(FR_OUT_pin18[0]), .pin4(FR_OUT_pin18[1]),
    .pin5(FR_OUT_pin18[1]), .pin6(FR_OUT_pin18[2]), .pin7(FR_OUT_pin18[2]), .pin8(FR_OUT_pin18[3]),
    .pin9(FR_OUT_pin18[3]), .pin10(1'b0), .pin11(LY), .pin12(FR_OUT_pin14[0]), .pin13(FR_OUT_pin14[0]),
    .pin14(FR_OUT_pin14[1]), .pin15(FR_OUT_pin14[1]), .pin16(FR_OUT_pin14[2]), .pin17(FR_OUT_pin14[2]),
    .pin18(FR_OUT_pin14[3]), .pin19(FR_OUT_pin14[3]), .pin20(1'b1));
  _74245 _74245_1 (
    .pin1(1'b1), .pin2(_74161_1_pin14[0]), .pin3(_74161_1_pin14[1]), .pin4(_74161_1_pin14[2]),
    .pin5(_74161_1_pin14[3]), .pin6(_74161_2_pin14[0]), .pin7(_74161_2_pin14[1]), .pin8(_74161_2_pin14[2]),
    .pin9(_74161_2_pin14[3]), .pin10(1'b0), .pin11(FR_OUT_pin14[3]), .pin12(FR_OUT_pin14[2]),
    .pin13(FR_OUT_pin14[1]), .pin14(FR_OUT_pin14[0]), .pin15(FR_OUT_pin18[3]), .pin16(FR_OUT_pin18[2]),
    .pin17(FR_OUT_pin18[1]), .pin18(FR_OUT_pin18[0]), .pin19(not_EPC_L), .pin20(1'b1));
  _74245 _74245_2 (
    .pin1(1'b1), .pin2(_74161_3_pin14[0]), .pin3(_74161_3_pin14[1]), .pin4(_74161_3_pin14[2]),
    .pin5(_74161_3_pin14[3]), .pin6(_74161_4_pin14[0]), .pin7(_74161_4_pin14[1]), .pin8(_74161_4_pin14[2]),
    .pin9(_74161_4_pin14[3]), .pin10(1'b0), .pin11(FR_OUT_pin14[3]), .pin12(FR_OUT_pin14[2]),
    .pin13(FR_OUT_pin14[1]), .pin14(FR_OUT_pin14[0]), .pin15(FR_OUT_pin18[3]), .pin16(FR_OUT_pin18[2]),
    .pin17(FR_OUT_pin18[1]), .pin18(FR_OUT_pin18[0]), .pin19(not_EPC_H), .pin20(1'b1));
  _74373 TMP (
    .pin1(not_ETMP), .pin2(FR_OUT_pin18[0]), .pin3(FR_OUT_pin18[0]), .pin4(FR_OUT_pin18[1]),
    .pin5(FR_OUT_pin18[1]), .pin6(FR_OUT_pin18[2]), .pin7(FR_OUT_pin18[2]), .pin8(FR_OUT_pin18[3]),
    .pin9(FR_OUT_pin18[3]), .pin10(1'b0), .pin11(LTMP), .pin12(FR_OUT_pin14[0]), .pin13(FR_OUT_pin14[0]),
    .pin14(FR_OUT_pin14[1]), .pin15(FR_OUT_pin14[1]), .pin16(FR_OUT_pin14[2]), .pin17(FR_OUT_pin14[2]),
    .pin18(FR_OUT_pin14[3]), .pin19(FR_OUT_pin14[3]), .pin20(1'b1));
  _74245 _74245_3 (
    .pin1(1'b1), .pin2(_74161_1_pin14[0]), .pin3(_74161_1_pin14[1]), .pin4(_74161_1_pin14[2]),
    .pin5(_74161_1_pin14[3]), .pin6(_74161_2_pin14[0]), .pin7(_74161_2_pin14[1]), .pin8(_74161_2_pin14[2]),
    .pin9(_74161_2_pin14[3]), .pin10(1'b0), .pin11(MAR_L_pin19), .pin12(MAR_L_pin16), .pin13(MAR_L_pin15),
    .pin14(MAR_L_pin12), .pin15(MAR_L_pin9), .pin16(MAR_L_pin6), .pin17(MAR_L_pin5), .pin18(MAR_L_pin2),
    .pin19(not_EPC_RAM), .pin20(1'b1));
  _74245 _74245_4 (
    .pin1(1'b1), .pin2(_74161_3_pin14[0]), .pin3(_74161_3_pin14[1]), .pin4(_74161_3_pin14[2]),
    .pin5(_74161_3_pin14[3]), .pin6(_74161_4_pin14[0]), .pin7(_74161_4_pin14[1]), .pin8(_74161_4_pin14[2]),
    .pin9(_74161_4_pin14[3]), .pin10(1'b0), .pin11(CLOCK_BUF_C27_pin13), .pin12(MAR_H_pin16),
    .pin13(MAR_H_pin15), .pin14(MAR_H_pin12), .pin15(MAR_H_pin9), .pin16(MAR_H_pin6), .pin17(MAR_H_pin5),
    .pin18(MAR_H_pin2), .pin19(not_EPC_RAM), .pin20(1'b1));
  // _28c256 ROM: pin names not known; wires that end beside it: MAR_H_pin16, MAR_H_pin12, MAR_L_pin19, MAR_L_pin16, MAR_L_pin15, MAR_L_pin12, MAR_L_pin9, MAR_L_pin6, MAR_L_pin5, MAR_L_pin2, FR_OUT_pin18[0], FR_OUT_pin18[1], FR_OUT_pin18[2], 1'b0, 1'b1, 1'b1, MAR_H_pin15, MAR_H_pin2, MAR_H_pin5, MAR_H_pin9, not_ERAM, MAR_H_pin6, CLOCK_BUF_C27_pin13, FR_OUT_pin14[3]
  // _62256 RAM: pin names not known; wires that end beside it: MAR_H_pin16, MAR_H_pin12, MAR_L_pin19, MAR_L_pin16, MAR_L_pin15, MAR_L_pin12, MAR_L_pin9, MAR_L_pin6, MAR_L_pin5, MAR_L_pin2, FR_OUT_pin18[0], FR_OUT_pin18[1], FR_OUT_pin18[2], 1'b0, 1'b1, not_WRAM, MAR_H_pin15, MAR_H_pin2, MAR_H_pin5, MAR_H_pin9, not_ERAM, MAR_H_pin6, CLOCK_BUF_C27_pin12, FR_OUT_pin14[3]
  _74245 _74245_5 (
    .pin1(1'b1), .pin2(1'b1), .pin3(1'b1), .pin4(1'b1), .pin5(1'b1), .pin6(1'b1), .pin7(1'b1), .pin8(1'b1),
    .pin9(1'b1), .pin10(1'b0), .pin11(CLOCK_BUF_C27_pin13), .pin12(MAR_H_pin16), .pin13(MAR_H_pin15),
    .pin14(MAR_H_pin12), .pin15(MAR_H_pin9), .pin16(MAR_H_pin6), .pin17(MAR_H_pin5), .pin18(MAR_H_pin2),
    .pin19(not_ESP), .pin20(1'b1));
  Seven_Seg_Hex seven_seg_hex_9 (.d(_74245_6_pin9), .dp(1'b0));
  Seven_Seg_Hex seven_seg_hex_10 (.d(_74245_6_pin5), .dp(1'b0));
  _74245 _74245_6 (
    .pin1(1'b1), .pin2(_74245_6_pin5[0]), .pin3(_74245_6_pin5[1]), .pin4(_74245_6_pin5[2]),
    .pin5(_74245_6_pin5[3]), .pin6(_74245_6_pin9[0]), .pin7(_74245_6_pin9[1]), .pin8(_74245_6_pin9[2]),
    .pin9(_74245_6_pin9[3]), .pin10(1'b0), .pin11(MAR_L_pin19), .pin12(MAR_L_pin16), .pin13(MAR_L_pin15),
    .pin14(MAR_L_pin12), .pin15(MAR_L_pin9), .pin16(MAR_L_pin6), .pin17(MAR_L_pin5), .pin18(MAR_L_pin2),
    .pin19(not_ESP), .pin20(1'b1));
  _74191 _74191_1 (
    .pin1(1'b1), .pin2(_74245_6_pin5[1]), .pin3(_74245_6_pin5[0]), .pin4(not_CSP), .pin5(SPD),
    .pin6(_74245_6_pin5[2]), .pin7(_74245_6_pin5[3]), .pin8(1'b0), .pin9(1'b1), .pin10(1'b1),
    .pin11(not_CLR), .pin13(_74191_1_pin13), .pin14(not_CLK), .pin15(1'b1), .pin16(1'b1));  // open: pin12
  _74191 _74191_2 (
    .pin1(1'b1), .pin2(_74245_6_pin9[1]), .pin3(_74245_6_pin9[0]), .pin4(not_CSP), .pin5(SPD),
    .pin6(_74245_6_pin9[2]), .pin7(_74245_6_pin9[3]), .pin8(1'b0), .pin9(1'b1), .pin10(1'b1),
    .pin11(not_CLR), .pin14(_74191_1_pin13), .pin15(1'b1), .pin16(1'b1));  // open: pin12, pin13

  // Notes on the sheet:
  //   NE555___CLK: Hz: 1000
  //   Int_NE555: Hz: 10
  //   CLK
  //   CHKI
  //   CHKI and Enable Int
  //   INT set
  //   not IR reset
  //   CLK/2
  //   not HLT
  //   contents of Control Word #3 (hex, n*v repeats v):
  //   /Users/Vittorio.Nardone/Documents/__private__/sap-project/roms/cw3-rom.hex false
  //   contents of Control Word #2 (hex, n*v repeats v):
  //   /Users/Vittorio.Nardone/Documents/__private__/sap-project/roms/cw2-rom.hex false
  //   contents of ROM (hex, n*v repeats v):
  //   /Users/Vittorio.Nardone/Documents/__private__/sap-project/roms/kernel-rom.hex false
  //   contents of Control Word #1 (hex, n*v repeats v):
  //   /Users/Vittorio.Nardone/Documents/__private__/sap-project/roms/cw1-rom.hex false
  //   contents of Control Word #7 (hex, n*v repeats v):
  //   /Users/Vittorio.Nardone/Documents/__private__/sap-project/roms/cw7-rom.hex false
  //   contents of Control Word #6 (hex, n*v repeats v):
  //   /Users/Vittorio.Nardone/Documents/__private__/sap-project/roms/cw6-rom.hex false
  //   contents of Control Word #5 (hex, n*v repeats v):
  //   /Users/Vittorio.Nardone/Documents/__private__/sap-project/roms/cw5-rom.hex false
  //   contents of Control Word #4 (hex, n*v repeats v):
  //   /Users/Vittorio.Nardone/Documents/__private__/sap-project/roms/cw4-rom.hex false
endmodule
